// Logisim project lab10part3.circ as structural Verilog: 2 circuits, main circuit main
module main (
);

  wire Batch_1_button_out, Batch_2_button_out, Batch_3_button_out, Batch_4_button_out, clock_1_out,
       cookiewatcher_1_cookiesdone, cookiewatcher_1_cookiesruined, cookiewatcher_2_cookiesdone,
       cookiewatcher_2_cookiesruined, cookiewatcher_3_cookiesdone, cookiewatcher_3_cookiesruined,
       cookiewatcher_4_cookiesdone, cookiewatcher_4_cookiesruined;

  Clock clock_1 (.out(clock_1_out));
  Button Batch_1_button (.out(Batch_1_button_out));
  Button Batch_2_button (.out(Batch_2_button_out));
  Button Batch_3_button (.out(Batch_3_button_out));
  Button Batch_4_button (.out(Batch_4_button_out));
  CookieWatcher cookiewatcher_1 (
    .CookieHandled(Batch_1_button_out), .ClockInput(clock_1_out),
    .CookiesRuined(cookiewatcher_1_cookiesruined), .CookiesDone(cookiewatcher_1_cookiesdone));
  CookieWatcher cookiewatcher_2 (
    .CookieHandled(Batch_2_button_out), .ClockInput(clock_1_out),
    .CookiesRuined(cookiewatcher_2_cookiesruined), .CookiesDone(cookiewatcher_2_cookiesdone));
  CookieWatcher cookiewatcher_3 (
    .CookieHandled(Batch_3_button_out), .ClockInput(clock_1_out),
    .CookiesRuined(cookiewatcher_3_cookiesruined), .CookiesDone(cookiewatcher_3_cookiesdone));
  CookieWatcher cookiewatcher_4 (
    .CookieHandled(Batch_4_button_out), .ClockInput(clock_1_out),
    .CookiesRuined(cookiewatcher_4_cookiesruined), .CookiesDone(cookiewatcher_4_cookiesdone));
  LED led_1 (.in(cookiewatcher_1_cookiesruined));
  LED led_2 (.in(cookiewatcher_1_cookiesdone));
  LED led_3 (.in(cookiewatcher_2_cookiesruined));
  LED led_4 (.in(cookiewatcher_2_cookiesdone));
  LED led_5 (.in(cookiewatcher_3_cookiesruined));
  LED led_6 (.in(cookiewatcher_3_cookiesdone));
  LED led_7 (.in(cookiewatcher_4_cookiesruined));
  LED led_8 (.in(cookiewatcher_4_cookiesdone));
endmodule

module CookieWatcher (
  input  CookieHandled,
  input  ClockInput,
  output CookiesRuined,
  output CookiesDone
);

  wire and_1_out, and_2_out, and_3_out, and_4_out, and_5_out, and_6_out;
  wire [6:0] counter_1_q;

  Counter counter_1 (
    .Q({CookiesDone, counter_1_q}), .clk(ClockInput), .clr(CookieHandled));  // open: load, D, count, carry
  and and_1 (and_1_out, counter_1_q[0], counter_1_q[1]);
  and and_2 (and_2_out, counter_1_q[2], counter_1_q[3]);
  and and_3 (and_3_out, counter_1_q[4], counter_1_q[5]);
  and and_4 (and_4_out, counter_1_q[6], CookiesDone);
  and and_5 (and_5_out, and_1_out, and_2_out);
  and and_6 (and_6_out, and_3_out, and_4_out);
  and and_7 (CookiesRuined, and_5_out, and_6_out);
endmodule
