// Logisim project lab10part5.circ as structural Verilog: 1 circuit, main circuit main
module main (
);

  wire clock_1_out, counter_1_carry, d_ff_1_qn;
  wire [7:0] controlled_buffer_1_out, counter_1_q, ram_1_data;

  Counter #(.ongoal("stay")) counter_1 (
    .Q(counter_1_q), .carry(counter_1_carry), .clk(clock_1_out));  // open: load, D, count, clr
  Clock clock_1 (.out(clock_1_out));
  assign controlled_buffer_1_out = d_ff_1_qn ? counter_1_q : 8'bz;  // Controlled_Buffer controlled_buffer_1
  D_Flip_Flop d_ff_1 (.clk(clock_1_out), .D(counter_1_carry), .Qn(d_ff_1_qn));  // open: Q, preset, en, reset
  RAM ram_1 (.addr(controlled_buffer_1_out), .data(ram_1_data), .clk(clock_1_out), .ld(1'b0));  // open: sel, clr
  assign ram_1_data = d_ff_1_qn ? 8'h61 : 8'bz;  // Controlled_Buffer controlled_buffer_2

  // Notes on the sheet:
  //   Delays stoping by 1/2 clock
endmodule
